# Fritzing sketch smart_home (saved by Fritzing 0.9.4)
breadboards: 1

parts:
  NodeMCU_v1 = NodeMCU v3 LoLin [part_number=ESP8266]
  Mod1 = KY-019 5V Relay Module [package="Breakout board"]
  buz1 = Piezo Buzzer
  S1 = KY-026
  DHT1 = DHT11 Humitidy and Temperature Sensor
  S2 = Pushbutton [package=THT]
  LED1 = smd LED [color="White (4500K)" package="0805 [SMD]"]
  R1 = Resistor [tolerance=±5% resistance=220 package="1206 [SMD]"]
  R2 = Resistor [tolerance=±5% resistance=1k package="2512 [SMD]"]
  Display1 = LCD screen 16x2 IIC [part_number=101290]
  R3 = Resistor [tolerance=±5% resistance=1k package="2512 [SMD]"]
  LED2 = LED - 3mm [color="Red (633nm)" package="3 mm [THT]"]
  R4 = Resistor [tolerance=±5% resistance=220 package="2512 [SMD]"]
  F1 = Fan - Ventilador [package=THT]
  VCC1 = Battery block 9V

nets:
  N1: NodeMCU_v1.D0, Mod1.S
  N2: NodeMCU_v1.D1, Display1.SCL
  N3: NodeMCU_v1.D2, Display1.SDA
  N4: NodeMCU_v1.D3, DHT1.DATA, R3.Pin_1
  N5: NodeMCU_v1.3V3, Mod1.+
  N6: NodeMCU_v1.GND#6, NodeMCU_v1.GND#33, Mod1.-
  N7: NodeMCU_v1.D5, buz1.pin_2, R4.Pin_1
  N8: NodeMCU_v1.D6, S2.leg0, R2.Pin_1
  N9: NodeMCU_v1.D7, S1.pin4
  N10: NodeMCU_v1.D8, R1.Pin_1
  VDD: NodeMCU_v1.VU, S1.pin3, DHT1.VDD, S2.leg1, Display1.VCC, R3.Pin_0
  GND: NodeMCU_v1.GND#41, buz1.pin_1, S1.pin2, DHT1.GND, LED1.cathode, R2.Pin_0, Display1.GND, LED2.cathode
  N11: Mod1.NC, VCC1.+
  N12: Mod1.Common, F1.5V
  N13: LED1.anode, R1.Pin_0
  N14: LED2.anode, R4.Pin_0
  N15: F1.GND, VCC1.-

custom parts:
  NodeMCU v3 LoLin: NodeMCU v3 LoLin NodeMCU (http://www.nodemcu.com/) is an open source IoT platform. It includes firmware (https://nodemcu-build.com/) which runs on the ESP8266 Wi-Fi SoC from Espressif Systems, and hardware which is based on the ESP-12E module. The term "NodeMCU" by default refers to the firmware rather than the dev kits. The firmware uses the Lua scripting language. It is based on the eLua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
  KY-019 5V Relay Module: KY-019 5V Relay module, used to control AC circuits. (Special thanks to vanepp for fixing the PCB holes and other errors)
  Piezo Buzzer: Part from https://www.nutsvolts.com/magazine/article/november2012_SmileysWorkshop modified to be .3 in spacing to match the adafruit buzzer 5V breadboard friendly part.
  KY-026: ky-026 flame sensor module
  DHT11 Humitidy and Temperature Sensor: DHT11 Humidity and Temperature Sensor
  LCD screen 16x2 IIC: LCD screen with HD44780 controller enables showing text, symbols, value or anything else that comes from Croduino/Arduino. It is capable of showing 16 symbols in two lines and therefore can be used in many projects that need to send clearly visible and legible output information.. • Color of symbols: White • Backlight: Blue • Dimensions: 80 x 36 x 12 mm • Screen dimensions: 64.5 x 16 mm •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
  Fan - Ventilador: Ventilador de 2 pines, se encuentra comunmente en computadoras de escritorio
  Battery block 9V: 9 Volt battery block with 200mil pcb footprint spacing
